// Logisim project stopwatch.circ as structural Verilog: 5 circuits, main circuit TP34
module TP34 (
);

  wire But_out, clk_out, Counter_d0, Counter_d1, Counter_d2, Counter_d3, Counter_d4, Counter_d5, Counter_d6,
       Counter_d7, Counter_d8, reset_out;
  wire [6:0] Controller1_disp, Controller2_disp, Controller3_disp;

  Clock clk (.out(clk_out));
  Button But (.out(But_out));
  Button reset (.out(reset_out));
  TP34Counter Counter (
    .Schedule(But_out), .Clock(clk_out), .Reset(reset_out), .D0(Counter_d0), .D1(Counter_d1),
    .D2(Counter_d2), .D3(Counter_d3), .D4(Counter_d4), .D5(Counter_d5), .D6(Counter_d6), .D7(Counter_d7),
    .D8(Counter_d8));
  LED Q02 (.in(Counter_d0));
  LED Q01 (.in(Counter_d1));
  LED Q12 (.in(Counter_d3));
  LED Q11 (.in(Counter_d4));
  LED Q22 (.in(Counter_d6));
  LED Q21 (.in(Counter_d7));
  LED Q00 (.in(Counter_d2));
  LED Q10 (.in(Counter_d5));
  LED Q20 (.in(Counter_d8));
  TP34DispController Controller1 (.N0(Counter_d0), .N1(Counter_d1), .N2(Counter_d2), .Disp(Controller1_disp));
  TP34DispController Controller2 (.N0(Counter_d3), .N1(Counter_d4), .N2(Counter_d5), .Disp(Controller2_disp));
  TP34DispController Controller3 (.N0(Counter_d6), .N1(Counter_d7), .N2(Counter_d8), .Disp(Controller3_disp));
  _7_Segment_Display Disp2 (
    .g(Controller3_disp[3]), .f(Controller3_disp[2]), .a(Controller3_disp[1]), .b(Controller3_disp[0]),
    .e(Controller3_disp[4]), .d(Controller3_disp[5]), .c(Controller3_disp[6]));  // open: dp
  _7_Segment_Display Disp1 (
    .g(Controller2_disp[3]), .f(Controller2_disp[2]), .a(Controller2_disp[1]), .b(Controller2_disp[0]),
    .e(Controller2_disp[4]), .d(Controller2_disp[5]), .c(Controller2_disp[6]));  // open: dp
  _7_Segment_Display Disp0 (
    .g(Controller1_disp[3]), .f(Controller1_disp[2]), .a(Controller1_disp[1]), .b(Controller1_disp[0]),
    .e(Controller1_disp[4]), .d(Controller1_disp[5]), .c(Controller1_disp[6]));  // open: dp
endmodule

module TP34Counter (
  input  Schedule,
  input  Clock,
  input  Reset,
  output D0,
  output D1,
  output D2,
  output D3,
  output D4,
  output D5,
  output D6,
  output D7,
  output D8
);

  wire and_1_out, and_2_out, and_3_out, and_4_out, and_5_out, and_6_out, and_7_out, and_8_out, and_9_out,
       and_10_out, and_11_out, and_12_out, and_13_out, and_14_out, and_15_out, and_16_out, and_17_out,
       and_18_out, and_19_out, and_20_out, and_21_out, and_22_out, and_23_out, and_24_out, and_25_out,
       and_26_out, and_27_out, and_28_out, and_29_out, and_30_out, and_31_out, and_32_out, and_33_out,
       and_34_out, and_35_out, and_36_out, and_37_out, and_38_out, and_39_out, and_40_out, and_41_out,
       and_42_out, and_43_out, and_44_out, and_45_out, and_46_out, and_47_out, and_48_out, and_49_out,
       and_50_out, d_ff_1_q, d_ff_2_q, d_ff_3_q, d_ff_4_q, d_ff_14_q, d_ff_15_q, not_1_out, not_2_out,
       not_3_out, not_4_out, not_5_out, not_6_out, not_7_out, not_8_out, not_9_out, not_10_out, not_11_out,
       not_12_out, not_13_out, not_14_out, not_15_out, not_16_out, not_17_out, not_18_out, not_19_out,
       not_20_out, not_21_out, not_22_out, not_23_out, not_24_out, not_25_out, not_26_out, not_27_out,
       not_28_out, not_29_out, not_30_out, not_31_out, not_32_out, not_33_out, not_34_out, not_35_out,
       not_36_out, not_37_out, not_38_out, not_39_out, not_40_out, not_41_out, not_42_out, not_43_out,
       not_44_out, not_45_out, not_46_out, not_47_out, not_48_out, not_49_out, not_50_out, not_51_out,
       not_52_out, not_53_out, not_54_out, not_55_out, not_56_out, not_57_out, not_58_out, not_59_out,
       not_60_out, not_61_out, not_62_out, not_63_out, not_64_out, not_65_out, not_66_out, not_67_out,
       not_68_out, not_69_out, not_70_out, not_71_out, not_72_out, not_73_out, not_74_out, not_75_out,
       not_76_out, not_77_out, not_78_out, not_79_out, not_80_out, not_81_out, not_82_out, not_83_out,
       not_84_out, not_85_out, not_86_out, not_87_out, not_88_out, not_89_out, not_90_out, not_91_out,
       not_92_out, not_93_out, not_94_out, not_95_out, not_96_out, not_97_out, not_98_out, not_99_out,
       not_100_out, not_101_out, not_102_out, O122_out, O124_out, or_1_out, or_2_out, or_3_out, or_4_out,
       or_5_out, or_6_out, or_7_out, or_8_out, or_9_out, or_10_out, or_11_out, or_12_out, or_13_out,
       or_14_out, or_15_out, or_16_out, or_17_out, or_18_out, or_19_out, or_20_out, or_21_out, or_22_out,
       or_23_out, or_24_out, or_25_out, or_26_out, or_27_out, or_28_out, or_29_out, or_30_out, or_31_out,
       or_32_out, or_33_out, SRLatch9_q, TP34SRLatch_1_q, TP34SRLatch_2_q, TP34SRLatch_3_q, TP34SRLatch_4_q,
       TP34SRLatch_5_q, TP34SRLatch_6_q, TP34SRLatch_7_q, TP34SRLatch_8_q, TP34SRLatch_9_q, xor_1_out,
       xor_2_out;
  wire [8:0] d_ff_5_q;

  D_Flip_Flop d_ff_1 (.D(Reset), .clk(Clock), .Q(d_ff_1_q));  // open: Qn, preset, reset
  D_Flip_Flop d_ff_2 (.D(Reset), .clk(Clock), .Q(d_ff_2_q));  // open: Qn, preset, reset
  D_Flip_Flop d_ff_3 (.D(Reset), .clk(Clock), .Q(d_ff_3_q));  // open: Qn, preset, reset
  not not_1 (not_1_out, d_ff_5_q[1]);
  not not_2 (not_2_out, d_ff_5_q[2]);
  not not_3 (not_3_out, Reset);
  not not_4 (not_4_out, d_ff_5_q[0]);
  not not_5 (not_5_out, d_ff_5_q[1]);
  not not_6 (not_6_out, Reset);
  not not_7 (not_7_out, d_ff_5_q[2]);
  not not_8 (not_8_out, Reset);
  not not_9 (not_9_out, d_ff_5_q[0]);
  not not_10 (not_10_out, Reset);
  not not_11 (not_11_out, Reset);
  not not_12 (not_12_out, d_ff_5_q[1]);
  not not_13 (not_13_out, d_ff_5_q[2]);
  not not_14 (not_14_out, Reset);
  not not_15 (not_15_out, xor_2_out);
  not not_16 (not_16_out, d_ff_5_q[0]);
  not not_17 (not_17_out, d_ff_5_q[1]);
  not not_18 (not_18_out, Reset);
  not not_19 (not_19_out, xor_2_out);
  not not_20 (not_20_out, d_ff_5_q[2]);
  not not_21 (not_21_out, Reset);
  not not_22 (not_22_out, xor_2_out);
  not not_23 (not_23_out, d_ff_5_q[0]);
  not not_24 (not_24_out, Reset);
  not not_25 (not_25_out, xor_2_out);
  not not_26 (not_26_out, Reset);
  not not_27 (not_27_out, xor_2_out);
  not not_28 (not_28_out, d_ff_5_q[4]);
  not not_29 (not_29_out, d_ff_5_q[5]);
  not not_30 (not_30_out, Reset);
  not not_31 (not_31_out, d_ff_5_q[3]);
  not not_32 (not_32_out, d_ff_5_q[4]);
  not not_33 (not_33_out, Reset);
  not not_34 (not_34_out, d_ff_5_q[5]);
  not not_35 (not_35_out, Reset);
  not not_36 (not_36_out, d_ff_5_q[3]);
  not not_37 (not_37_out, Reset);
  not not_38 (not_38_out, Reset);
  not not_39 (not_39_out, d_ff_5_q[4]);
  not not_40 (not_40_out, d_ff_5_q[5]);
  not not_41 (not_41_out, Reset);
  not not_42 (not_42_out, xor_2_out);
  not not_43 (not_43_out, d_ff_5_q[3]);
  not not_44 (not_44_out, d_ff_5_q[4]);
  not not_45 (not_45_out, Reset);
  not not_46 (not_46_out, xor_2_out);
  not not_47 (not_47_out, d_ff_5_q[5]);
  not not_48 (not_48_out, Reset);
  not not_49 (not_49_out, xor_2_out);
  not not_50 (not_50_out, d_ff_5_q[3]);
  not not_51 (not_51_out, Reset);
  not not_52 (not_52_out, xor_2_out);
  not not_53 (not_53_out, Reset);
  not not_54 (not_54_out, xor_2_out);
  not not_55 (not_55_out, d_ff_5_q[7]);
  not not_56 (not_56_out, d_ff_5_q[8]);
  not not_57 (not_57_out, Reset);
  not not_58 (not_58_out, d_ff_5_q[6]);
  not not_59 (not_59_out, d_ff_5_q[7]);
  not not_60 (not_60_out, Reset);
  not not_61 (not_61_out, d_ff_5_q[8]);
  not not_62 (not_62_out, Reset);
  not not_63 (not_63_out, d_ff_5_q[6]);
  not not_64 (not_64_out, Reset);
  not not_65 (not_65_out, Reset);
  not not_66 (not_66_out, d_ff_5_q[7]);
  not not_67 (not_67_out, d_ff_5_q[8]);
  not not_68 (not_68_out, Reset);
  not not_69 (not_69_out, xor_2_out);
  not not_70 (not_70_out, d_ff_5_q[6]);
  not not_71 (not_71_out, d_ff_5_q[7]);
  not not_72 (not_72_out, Reset);
  not not_73 (not_73_out, xor_2_out);
  not not_74 (not_74_out, d_ff_5_q[8]);
  not not_75 (not_75_out, Reset);
  not not_76 (not_76_out, xor_2_out);
  not not_77 (not_77_out, d_ff_5_q[6]);
  not not_78 (not_78_out, Reset);
  not not_79 (not_79_out, xor_2_out);
  not not_80 (not_80_out, Reset);
  not not_81 (not_81_out, xor_2_out);
  and and_1 (and_1_out, d_ff_5_q[0], not_1_out, not_2_out, not_3_out, xor_2_out);
  and and_2 (and_2_out, not_4_out, not_5_out, d_ff_5_q[2], not_6_out, xor_2_out);
  and and_3 (and_3_out, d_ff_5_q[0], d_ff_5_q[1], not_7_out, not_8_out, xor_2_out);
  and and_4 (and_4_out, not_9_out, d_ff_5_q[1], d_ff_5_q[2], not_10_out, xor_2_out);
  and and_5 (and_5_out, d_ff_5_q[0], d_ff_5_q[1], d_ff_5_q[2], not_11_out, xor_2_out);
  and and_6 (and_6_out, d_ff_1_q, Reset);
  and and_7 (and_7_out, d_ff_5_q[0], not_12_out, not_13_out, not_14_out, not_15_out);
  and and_8 (and_8_out, not_16_out, not_17_out, d_ff_5_q[2], not_18_out, not_19_out);
  and and_9 (and_9_out, d_ff_5_q[0], d_ff_5_q[1], not_20_out, not_21_out, not_22_out);
  and and_10 (and_10_out, not_23_out, d_ff_5_q[1], d_ff_5_q[2], not_24_out, not_25_out);
  and and_11 (and_11_out, d_ff_5_q[0], d_ff_5_q[1], d_ff_5_q[2], not_26_out, not_27_out);
  and and_12 (and_12_out, d_ff_5_q[3], not_28_out, not_29_out, not_30_out, xor_2_out);
  and and_13 (and_13_out, not_31_out, not_32_out, d_ff_5_q[5], not_33_out, xor_2_out);
  and and_14 (and_14_out, d_ff_5_q[3], d_ff_5_q[4], not_34_out, not_35_out, xor_2_out);
  and and_15 (and_15_out, not_36_out, d_ff_5_q[4], d_ff_5_q[5], not_37_out, xor_2_out);
  and and_16 (and_16_out, d_ff_5_q[3], d_ff_5_q[4], d_ff_5_q[5], not_38_out, xor_2_out);
  and and_17 (and_17_out, d_ff_2_q, Reset);
  and and_18 (and_18_out, d_ff_5_q[3], not_39_out, not_40_out, not_41_out, not_42_out);
  and and_19 (and_19_out, not_43_out, not_44_out, d_ff_5_q[5], not_45_out, not_46_out);
  and and_20 (and_20_out, d_ff_5_q[3], d_ff_5_q[4], not_47_out, not_48_out, not_49_out);
  and and_21 (and_21_out, not_50_out, d_ff_5_q[4], d_ff_5_q[5], not_51_out, not_52_out);
  and and_22 (and_22_out, d_ff_5_q[3], d_ff_5_q[4], d_ff_5_q[5], not_53_out, not_54_out);
  and and_23 (and_23_out, d_ff_5_q[6], not_55_out, not_56_out, not_57_out, xor_2_out);
  and and_24 (and_24_out, not_58_out, not_59_out, d_ff_5_q[8], not_60_out, xor_2_out);
  and and_25 (and_25_out, d_ff_5_q[6], d_ff_5_q[7], not_61_out, not_62_out, xor_2_out);
  and and_26 (and_26_out, not_63_out, d_ff_5_q[7], d_ff_5_q[8], not_64_out, xor_2_out);
  and and_27 (and_27_out, d_ff_5_q[6], d_ff_5_q[7], d_ff_5_q[8], not_65_out, xor_2_out);
  and and_28 (and_28_out, d_ff_3_q, Reset);
  and and_29 (and_29_out, d_ff_5_q[6], not_66_out, not_67_out, not_68_out, not_69_out);
  and and_30 (and_30_out, not_70_out, not_71_out, d_ff_5_q[8], not_72_out, not_73_out);
  and and_31 (and_31_out, d_ff_5_q[6], d_ff_5_q[7], not_74_out, not_75_out, not_76_out);
  and and_32 (and_32_out, not_77_out, d_ff_5_q[7], d_ff_5_q[8], not_78_out, not_79_out);
  and and_33 (and_33_out, d_ff_5_q[6], d_ff_5_q[7], d_ff_5_q[8], not_80_out, not_81_out);
  or or_1 (or_1_out, and_1_out, and_11_out, and_3_out, and_9_out);
  or or_2 (or_2_out, and_2_out, and_4_out, and_7_out, and_8_out, and_10_out, and_5_out);
  or or_3 (or_3_out, and_9_out, and_1_out, and_5_out, and_8_out);
  or or_4 (or_4_out, and_2_out, and_7_out, and_3_out, and_11_out);
  or or_5 (or_5_out, and_2_out, and_8_out, and_5_out, and_10_out);
  or or_6 (or_6_out, and_1_out, and_7_out, and_11_out, and_9_out, and_3_out, and_4_out);
  or or_7 (or_7_out, and_12_out, and_22_out, and_14_out, and_20_out);
  or or_8 (or_8_out, and_13_out, and_15_out, and_18_out, and_19_out, and_21_out, and_16_out);
  or or_9 (or_9_out, and_20_out, and_12_out, and_16_out, and_19_out);
  or or_10 (or_10_out, and_13_out, and_18_out, and_14_out, and_22_out);
  or or_11 (or_11_out, and_13_out, and_19_out, and_16_out, and_21_out);
  or or_12 (or_12_out, and_12_out, and_18_out, and_22_out, and_20_out, and_14_out, and_15_out);
  or or_13 (or_13_out, and_23_out, and_33_out, and_25_out, and_31_out);
  or or_14 (or_14_out, and_24_out, and_26_out, and_29_out, and_30_out, and_32_out, and_27_out);
  or or_15 (or_15_out, and_31_out, and_23_out, and_27_out, and_30_out);
  or or_16 (or_16_out, and_24_out, and_29_out, and_25_out, and_33_out);
  or or_17 (or_17_out, and_24_out, and_30_out, and_27_out, and_32_out);
  or or_18 (or_18_out, and_23_out, and_29_out, and_33_out, and_31_out, and_25_out, and_26_out);
  or or_19 (or_19_out, or_2_out, and_6_out);
  or or_20 (or_20_out, and_6_out, or_4_out);
  or or_21 (or_21_out, and_6_out, or_5_out);
  or or_22 (or_22_out, and_17_out, or_8_out);
  or or_23 (or_23_out, and_17_out, or_9_out);
  or or_24 (or_24_out, and_17_out, or_11_out);
  or or_25 (or_25_out, and_28_out, or_14_out);
  or or_26 (or_26_out, and_28_out, or_16_out);
  or or_27 (or_27_out, and_28_out, or_17_out);
  D_Flip_Flop d_ff_4 (.D(Reset), .clk(Clock), .Q(d_ff_4_q));  // open: Qn, preset, reset
  TP34SRLatch TP34SRLatch_1 (.R(or_1_out), .S(or_19_out), .Q(TP34SRLatch_1_q));
  TP34SRLatch TP34SRLatch_2 (.R(or_3_out), .S(or_20_out), .Q(TP34SRLatch_2_q));
  TP34SRLatch TP34SRLatch_3 (.R(or_21_out), .S(or_6_out), .Q(TP34SRLatch_3_q));
  TP34SRLatch TP34SRLatch_4 (.R(or_7_out), .S(or_22_out), .Q(TP34SRLatch_4_q));
  TP34SRLatch TP34SRLatch_5 (.R(or_23_out), .S(or_10_out), .Q(TP34SRLatch_5_q));
  TP34SRLatch TP34SRLatch_6 (.R(or_24_out), .S(or_12_out), .Q(TP34SRLatch_6_q));
  TP34SRLatch TP34SRLatch_7 (.R(or_13_out), .S(or_25_out), .Q(TP34SRLatch_7_q));
  TP34SRLatch TP34SRLatch_8 (.R(or_15_out), .S(or_26_out), .Q(TP34SRLatch_8_q));
  TP34SRLatch TP34SRLatch_9 (.R(or_27_out), .S(or_18_out), .Q(TP34SRLatch_9_q));
  and and_34 (and_34_out, d_ff_4_q, TP34SRLatch_1_q);
  D_Flip_Flop d_ff_5 (.D(TP34SRLatch_1_q), .clk(Clock), .Q(d_ff_5_q[0]), .preset(and_34_out));  // open: Qn, reset
  and and_35 (and_35_out, d_ff_4_q, TP34SRLatch_2_q);
  D_Flip_Flop d_ff_6 (.D(TP34SRLatch_2_q), .clk(Clock), .Q(d_ff_5_q[1]), .preset(and_35_out));  // open: Qn, reset
  D_Flip_Flop d_ff_7 (.D(TP34SRLatch_3_q), .clk(Clock), .Q(d_ff_5_q[2]), .reset(and_36_out));  // open: Qn, preset
  and and_36 (and_36_out, d_ff_4_q, not_82_out);
  not not_82 (not_82_out, TP34SRLatch_3_q);
  not not_83 (not_83_out, d_ff_5_q[1]);
  not not_84 (not_84_out, d_ff_5_q[2]);
  and and_37 (and_37_out, xor_2_out, d_ff_5_q[0], not_83_out, not_84_out);
  and and_38 (and_38_out, TP34SRLatch_4_q, d_ff_4_q);
  D_Flip_Flop d_ff_8 (.D(TP34SRLatch_4_q), .clk(or_28_out), .Q(d_ff_5_q[3]), .preset(and_38_out));  // open: Qn, reset
  D_Flip_Flop d_ff_9 (.D(TP34SRLatch_5_q), .clk(or_28_out), .Q(d_ff_5_q[4]), .reset(and_39_out));  // open: Qn, preset
  not not_85 (not_85_out, TP34SRLatch_5_q);
  and and_39 (and_39_out, not_85_out, d_ff_4_q);
  D_Flip_Flop d_ff_10 (.D(TP34SRLatch_6_q), .clk(or_28_out), .Q(d_ff_5_q[5]), .reset(and_40_out));  // open: Qn, preset
  not not_86 (not_86_out, TP34SRLatch_6_q);
  and and_40 (and_40_out, not_86_out, d_ff_4_q);
  not not_87 (not_87_out, d_ff_5_q[4]);
  not not_88 (not_88_out, d_ff_5_q[5]);
  and and_41 (and_41_out, xor_2_out, d_ff_5_q[3], not_87_out, not_88_out);
  and and_42 (and_42_out, TP34SRLatch_7_q, d_ff_4_q);
  D_Flip_Flop d_ff_11 (.D(TP34SRLatch_7_q), .clk(or_29_out), .Q(d_ff_5_q[6]), .preset(and_42_out));  // open: Qn, reset
  and and_43 (and_43_out, TP34SRLatch_8_q, d_ff_4_q);
  D_Flip_Flop d_ff_12 (.D(TP34SRLatch_8_q), .clk(or_29_out), .Q(d_ff_5_q[7]), .preset(and_43_out));  // open: Qn, reset
  D_Flip_Flop d_ff_13 (.D(TP34SRLatch_9_q), .clk(or_29_out), .Q(d_ff_5_q[8]), .reset(and_44_out));  // open: Qn, preset
  not not_89 (not_89_out, TP34SRLatch_9_q);
  and and_44 (and_44_out, not_89_out, d_ff_4_q);
  not not_90 (not_90_out, xor_2_out);
  and and_45 (and_45_out, not_90_out, d_ff_5_q[0], d_ff_5_q[1], d_ff_5_q[2]);
  or or_28 (or_28_out, and_37_out, and_45_out);
  not not_91 (not_91_out, xor_2_out);
  and and_46 (and_46_out, not_91_out, d_ff_5_q[3], d_ff_5_q[4], d_ff_5_q[5]);
  or or_29 (or_29_out, and_41_out, and_46_out);
  not not_92 (not_92_out, d_ff_5_q[2]);
  and O122 (O122_out, xor_2_out, d_ff_5_q[0], d_ff_5_q[1], not_92_out, d_ff_5_q[3], d_ff_5_q[4], not_93_out, not_94_out, not_95_out, d_ff_5_q[8]);
  not not_93 (not_93_out, d_ff_5_q[5]);
  not not_94 (not_94_out, d_ff_5_q[6]);
  not not_95 (not_95_out, d_ff_5_q[7]);
  not not_96 (not_96_out, xor_2_out);
  and O124 (O124_out, not_96_out, d_ff_5_q[0], d_ff_5_q[1], d_ff_5_q[2], d_ff_5_q[3], d_ff_5_q[4], not_97_out, not_98_out, not_99_out, d_ff_5_q[8]);
  not not_97 (not_97_out, d_ff_5_q[5]);
  not not_98 (not_98_out, d_ff_5_q[6]);
  not not_99 (not_99_out, d_ff_5_q[7]);
  or or_30 (or_30_out, O122_out, O124_out);
  xor xor_1 (xor_1_out, or_31_out, 1'b1);
  and and_47 (and_47_out, Schedule, not_100_out);
  not not_100 (not_100_out, or_30_out);
  or or_31 (or_31_out, and_47_out, and_48_out);
  or or_32 (or_32_out, xor_1_out, Reset);
  TP34Condition TP34Condition_1 (.Input_bus_1(d_ff_5_q), .Output_bus_1({D8, D7, D6, D5, D4, D3, D2, D1, D0}));
  not not_101 (not_101_out, d_ff_14_q);
  and and_48 (and_48_out, not_101_out, SRLatch9_q);
  and and_49 (and_49_out, Reset, not_102_out);
  not not_102 (not_102_out, xor_2_out);
  TP34SRLatch SRLatch9 (.R(or_32_out), .S(and_47_out), .Q(SRLatch9_q));
  and and_50 (and_50_out, SRLatch9_q, or_30_out);
  D_Flip_Flop d_ff_14 (.D(and_50_out), .clk(Clock), .Q(d_ff_14_q), .reset(Reset));  // open: Qn, preset
  xor xor_2 (xor_2_out, d_ff_15_q, 1'b1);
  D_Flip_Flop d_ff_15 (.D(xor_2_out), .clk(or_33_out), .Q(d_ff_15_q), .reset(Reset));  // open: Qn, preset
  or or_33 (or_33_out, d_ff_14_q, and_49_out);
endmodule

module TP34SRLatch (
  input  R,
  input  S,
  output Q
);

  wire nor_2_out;

  nor nor_1 (Q, R, nor_2_out);
  nor nor_2 (nor_2_out, Q, S);
endmodule

module TP34DispController (
  input  N0,
  input  N1,
  input  N2,
  output [6:0] Disp
);

  wire and_1_out, and_2_out, and_3_out, and_4_out, and_5_out, not_1_out, not_2_out, not_3_out, not_4_out,
       not_5_out, not_6_out;

  not not_1 (not_1_out, N1);
  not not_2 (not_2_out, N2);
  not not_3 (not_3_out, N0);
  not not_4 (not_4_out, N1);
  not not_5 (not_5_out, N2);
  not not_6 (not_6_out, N0);
  and and_1 (and_1_out, N0, not_1_out, not_2_out);
  and and_2 (and_2_out, not_3_out, not_4_out, N2);
  and and_3 (and_3_out, N0, N1, not_5_out);
  and and_4 (and_4_out, not_6_out, N1, N2);
  and and_5 (and_5_out, N0, N1, N2);
  or or_1 (Disp[0], and_4_out, and_1_out, and_5_out, and_3_out, and_2_out);
  or or_2 (Disp[1], and_1_out, and_3_out, and_4_out);
  or or_3 (Disp[2], and_1_out, and_5_out);
  or or_4 (Disp[3], and_3_out, and_4_out, and_5_out);
  or or_5 (Disp[4], and_1_out, and_3_out);
  or or_6 (Disp[6], and_1_out, and_5_out, and_4_out, and_2_out);
  or or_7 (Disp[5], and_1_out, and_3_out, and_4_out);
endmodule

module TP34Condition (
  input  [8:0] Input_bus_1,
  output [8:0] Output_bus_1
);

  wire not_1_out, not_2_out, not_3_out;

  not not_1 (not_1_out, Input_bus_1[2]);
  not not_2 (not_2_out, Input_bus_1[5]);
  not not_3 (not_3_out, Input_bus_1[8]);
  or or_1 (Output_bus_1[0], not_1_out, Input_bus_1[0]);
  or or_2 (Output_bus_1[3], Input_bus_1[3], not_2_out);
  or or_3 (Output_bus_1[6], Input_bus_1[6], not_3_out);

  assign {Output_bus_1[8:7], Output_bus_1[5:4], Output_bus_1[2:1]} = {Input_bus_1[8:7], Input_bus_1[5:4], Input_bus_1[2:1]};
endmodule
